// Logisim project hw3.circ as structural Verilog: 5 circuits, main circuit 1-Bit Adder
module _1_Bit_Adder (
  input  B,
  input  A,
  input  Carry_In,
  output Carry_Out,
  output Output
);

  wire and_1_out, and_2_out, and_3_out, and_4_out, and_5_out, and_6_out, and_7_out;

  and and_1 (and_1_out, ~A, B, Carry_In);  // AND_Gate
  and and_2 (and_2_out, A, ~B, Carry_In);  // AND_Gate
  or or_1 (Carry_Out, and_1_out, and_2_out, and_3_out, and_4_out);
  and and_3 (and_3_out, A, B, ~Carry_In);  // AND_Gate
  and and_4 (and_4_out, A, B, Carry_In);
  and and_5 (and_5_out, ~A, ~B, Carry_In);  // AND_Gate
  and and_6 (and_6_out, ~A, B, ~Carry_In);  // AND_Gate
  or or_2 (Output, and_4_out, and_5_out, and_6_out, and_7_out);
  and and_7 (and_7_out, A, ~B, ~Carry_In);  // AND_Gate

  // Notes on the sheet:
  //   1-Bit Adder
endmodule

module _4___Bit_Adder (
  input  [3:0] A,
  input  [3:0] B,
  input  CARRY_IN,
  output CARRY_OUT,
  output [3:0] OUTPUT
);

  wire n1_bit_adder_2_carry_out, n1_bit_adder_3_carry_out, n1_bit_adder_4_carry_out;

  _1_Bit_Adder u_1_bit_adder_1 (
    .A(A[3]), .B(B[3]), .Carry_Out(CARRY_OUT), .Output(OUTPUT[3]), .Carry_In(n1_bit_adder_2_carry_out));
  _1_Bit_Adder u_1_bit_adder_2 (
    .A(A[2]), .B(B[2]), .Carry_Out(n1_bit_adder_2_carry_out), .Output(OUTPUT[2]),
    .Carry_In(n1_bit_adder_3_carry_out));
  _1_Bit_Adder u_1_bit_adder_3 (
    .A(A[1]), .B(B[1]), .Carry_Out(n1_bit_adder_3_carry_out), .Output(OUTPUT[1]),
    .Carry_In(n1_bit_adder_4_carry_out));
  _1_Bit_Adder u_1_bit_adder_4 (
    .A(A[0]), .B(B[0]), .Carry_Out(n1_bit_adder_4_carry_out), .Output(OUTPUT[0]), .Carry_In(CARRY_IN));
endmodule

module _4_BIT_ALU (
  input  [3:0] in_1,
  input  [3:0] in_2,
  input  CARRY_IN,
  input  [2:0] in_4,
  output CARRY_OUT,
  output [3:0] OUTPUT
);

  wire C_Out;
  wire [3:0] _2_s_Comp, A___1, A___B, A___B_t, nA, not_1_out, not_2_out, Subtract, Sum;

  Multiplexer #(.select(3), .width(4), .disabled(0), .enable("false")) multiplexer_1 (
    .in0(Sum), .in1(Subtract), .in2(A___1), .in3(_2_s_Comp), .in4({in_1[0], 3'b000}), .in5(A___B), .in6(nA),
    .in7(A___B_t), .out(OUTPUT), .sel(in_4));
  and and_1 (CARRY_OUT, C_Out, ~in_4[0], ~in_4[1], ~in_4[2]);  // AND_Gate
  _4___Bit_Adder u_4_bit_adder_1 (.CARRY_OUT(C_Out), .A(in_1), .B(in_2), .OUTPUT(Sum), .CARRY_IN(CARRY_IN));
  assign not_1_out = ~in_2;  // NOT_Gate not_1, 4 bits wide
  _4___Bit_Adder u_4_bit_adder_2 (.A(in_1), .B(not_1_out), .OUTPUT(Subtract), .CARRY_IN(1'b1));  // open: CARRY_OUT
  _4___Bit_Adder u_4_bit_adder_3 (.A(in_1), .B(4'b0001), .OUTPUT(A___1), .CARRY_IN(1'b0));  // open: CARRY_OUT
  assign not_2_out = ~in_1;  // NOT_Gate not_2, 4 bits wide
  _4___Bit_Adder u_4_bit_adder_4 (.A(not_2_out), .B(4'b0001), .OUTPUT(_2_s_Comp), .CARRY_IN(1'b0));  // open: CARRY_OUT
  assign A___B = in_1 & in_2;  // AND_Gate and_2, 4 bits wide
  assign nA = ~in_1;  // NOT_Gate not_3, 4 bits wide
  assign A___B_t = in_1 ^ in_2;  // XOR_Gate xor_1, 4 bits wide

  // Other names for the same wires on the sheet: A[3:0] = in_1; A___8[3] = in_1[0]; B[3:0] = in_2;
  //   Controls[2:0] = in_4; Out[3:0] = OUTPUT

  // Notes on the sheet:
  //   000 - SUM
  //   010 - A + 1
  //   100 - A * 8
  //   101 - A & B
  //   110 - ~A
  //   111 - A ^ B
  //   001 - SUBTRACT
  //   011 - 2'S COMPLEMENT
endmodule

module _16_Bit_Adder (
  input  [15:0] in_1,
  input  [15:0] in_2,
  input  in_3,
  output out_4,
  output [15:0] out_5
);

  wire n4_bit_adder_2_carry_out, n4_bit_adder_3_carry_out, n4_bit_adder_4_carry_out;

  _4___Bit_Adder u_4_bit_adder_1 (
    .CARRY_OUT(out_4), .A(in_1[15:12]), .B(in_2[15:12]), .OUTPUT(out_5[15:12]),
    .CARRY_IN(n4_bit_adder_2_carry_out));
  _4___Bit_Adder u_4_bit_adder_2 (
    .CARRY_OUT(n4_bit_adder_2_carry_out), .A(in_1[11:8]), .B(in_2[11:8]), .OUTPUT(out_5[11:8]),
    .CARRY_IN(n4_bit_adder_3_carry_out));
  _4___Bit_Adder u_4_bit_adder_3 (
    .CARRY_OUT(n4_bit_adder_3_carry_out), .A(in_1[7:4]), .B(in_2[7:4]), .OUTPUT(out_5[7:4]),
    .CARRY_IN(n4_bit_adder_4_carry_out));
  _4___Bit_Adder u_4_bit_adder_4 (
    .CARRY_OUT(n4_bit_adder_4_carry_out), .A(in_1[3:0]), .B(in_2[3:0]), .OUTPUT(out_5[3:0]), .CARRY_IN(in_3));
endmodule

module _16_Bit_ALU (
  input  [15:0] in_1,
  input  [15:0] in_2,
  input  CARRY_IN,
  input  [2:0] in_4,
  output CARRY_OUT,
  output [15:0] OUTPUT
);

  wire C_Out;
  wire [15:0] _2_s_Comp, A___1, A___B, A___B_t, nA, not_1_out, not_2_out, Subtract, Sum;

  Multiplexer #(.select(3), .width(16), .disabled(0), .enable("false")) multiplexer_1 (
    .in0(Sum), .in1(Subtract), .in2(A___1), .in3(_2_s_Comp), .in4({in_1[12:0], 3'b000}), .in5(A___B),
    .in6(nA), .in7(A___B_t), .out(OUTPUT), .sel(in_4));
  and and_1 (CARRY_OUT, C_Out, ~in_4[0], ~in_4[1], ~in_4[2]);  // AND_Gate
  _16_Bit_Adder u_16_bit_adder_1 (.out_4(C_Out), .in_1(in_1), .in_2(in_2), .out_5(Sum), .in_3(CARRY_IN));
  assign not_1_out = ~in_2;  // NOT_Gate not_1, 16 bits wide
  _16_Bit_Adder u_16_bit_adder_2 (.in_1(in_1), .in_2(not_1_out), .out_5(Subtract), .in_3(1'b1));  // open: out_4
  _16_Bit_Adder u_16_bit_adder_3 (.in_1(in_1), .in_2(16'h1), .out_5(A___1), .in_3(1'b0));  // open: out_4
  assign not_2_out = ~in_1;  // NOT_Gate not_2, 16 bits wide
  _16_Bit_Adder u_16_bit_adder_4 (.in_1(not_2_out), .in_2(16'h1), .out_5(_2_s_Comp), .in_3(1'b0));  // open: out_4
  assign A___B = in_1 & in_2;  // AND_Gate and_2, 16 bits wide
  assign nA = ~in_1;  // NOT_Gate not_3, 16 bits wide
  assign A___B_t = in_1 ^ in_2;  // XOR_Gate xor_1, 16 bits wide

  // Other names for the same wires on the sheet: A[15:0] = in_1; A___8[15:3] = in_1[12:0]; B[15:0] = in_2;
  //   Controls[2:0] = in_4; Out[15:0] = OUTPUT

  // Notes on the sheet:
  //   000 - SUM
  //   010 - A + 1
  //   100 - A * 8
  //   101 - A & B
  //   110 - ~A
  //   111 - A ^ B
  //   001 - SUBTRACT
  //   011 - 2'S COMPLEMENT
endmodule
