// Logisim project hw4.circ as structural Verilog: 5 circuits, main circuit one hot state machine
module one_hot_state_machine (
  input  G,
  input  Clock,
  input  Reset,
  output W,
  output X,
  output Y,
  output Z
);

  wire and_2_out, and_4_out, and_5_out, and_6_out, and_7_out, and_8_out, and_9_out, and_10_out, and_11_out,
       Cond0, Cond1, Cond2, Cond3, Cond4, Cond5, S0, S1, S2, S3, S4, S5, Start;

  and and_1 (Start, ~S0, ~S1, ~S2, ~S5, ~S4, ~S3);  // AND_Gate
  or or_1 (Cond0, Start, and_2_out);
  and and_2 (and_2_out, S3, ~G);  // AND_Gate
  and and_3 (Cond1, S0, G);
  and and_4 (and_4_out, S0, ~G);  // AND_Gate
  or or_2 (Cond2, S1, and_4_out, and_5_out);
  and and_5 (and_5_out, S5, ~G);  // AND_Gate
  and and_6 (and_6_out, S2, G);
  or or_3 (Cond3, and_6_out, and_7_out);
  and and_7 (and_7_out, S5, G);
  and and_8 (and_8_out, S4, ~G);  // AND_Gate
  or or_4 (Cond4, and_8_out, and_9_out);
  and and_9 (and_9_out, S2, ~G);  // AND_Gate
  and and_10 (and_10_out, S3, G);
  or or_5 (Cond5, and_10_out, and_11_out);
  and and_11 (and_11_out, S4, G);
  Register #(.width(6)) register_1 (
    .D({Cond5, Cond4, Cond3, Cond2, Cond1, Cond0}), .Q({S5, S4, S3, S2, S1, S0}), .clk(Clock), .clr(Reset));  // open: en
  or or_6 (W, S1, S3, S5);
  or or_7 (X, S0, S2, S5);
  or or_8 (Y, S2, S3, S5);
  or or_9 (Z, S4, S5);

  // Other names for the same wires on the sheet: CLK = Clock; RST = Reset

  // Notes on the sheet:
  //   Name: Hussain Mumtaz
  //   Your One-hot State Machine
  //   DO NOT move or change these pins.
endmodule

module one_hot_tester (
  input  G
);

  wire CLK_out, one_hot_state_machine_1_w, one_hot_state_machine_1_x, one_hot_state_machine_1_y,
       one_hot_state_machine_1_z, RST_out;

  Clock CLK (.out(CLK_out));
  LED led_1 (.in(one_hot_state_machine_1_w));
  one_hot_state_machine one_hot_state_machine_1 (
    .W(one_hot_state_machine_1_w), .G(G), .X(one_hot_state_machine_1_x), .Clock(CLK_out),
    .Y(one_hot_state_machine_1_y), .Reset(RST_out), .Z(one_hot_state_machine_1_z));
  LED led_2 (.in(one_hot_state_machine_1_x));
  LED led_3 (.in(one_hot_state_machine_1_y));
  LED led_4 (.in(one_hot_state_machine_1_z));
  Button RST (.out(RST_out));
endmodule

module reduced_state_machine (
  input  G,
  input  Clock,
  input  Reset,
  output W,
  output X,
  output Y,
  output Z
);

  wire and_1_out, and_2_out, and_3_out, and_4_out, and_5_out, and_6_out, and_7_out, and_8_out, and_9_out,
       and_10_out, and_11_out, and_12_out, Cond0, Cond1, Cond2, N1;

  and and_1 (and_1_out, ~G, N1, ~W);  // AND_Gate
  and and_2 (and_2_out, Z, ~W);  // AND_Gate
  and and_3 (and_3_out, G, N1, W);
  and and_4 (and_4_out, ~G, ~Z, ~N1);  // AND_Gate
  and and_5 (and_5_out, ~N1, W);  // AND_Gate
  and and_6 (and_6_out, G, N1, ~W);  // AND_Gate
  and and_7 (and_7_out, G, Z);
  and and_8 (and_8_out, G, N1);
  and and_9 (and_9_out, G, ~W);  // AND_Gate
  and and_10 (and_10_out, ~Z, ~W);  // AND_Gate
  and and_11 (and_11_out, Z, W);
  and and_12 (and_12_out, Z, W);
  or or_1 (Cond2, and_1_out, and_2_out, and_3_out);
  or or_2 (Cond1, and_4_out, and_5_out, and_6_out);
  or or_3 (Cond0, and_7_out, and_8_out, and_9_out);
  or or_4 (X, and_10_out, and_11_out);
  or or_5 (Y, N1, and_12_out);
  Register #(.width(3)) register_1 (.D({Cond2, Cond1, Cond0}), .Q({Z, N1, W}), .clk(Clock), .clr(Reset));  // open: en

  // Other names for the same wires on the sheet: N0 = W; N2 = Z; CLK = Clock; RST = Reset

  // Notes on the sheet:
  //   Your Reduced State Machine
  //   Name: Hussain Mumtaz
  //   DO NOT move or change these pins.
endmodule

module reduced_tester (
  input  G
);

  wire CLK_out, reduced_state_machine_1_w, reduced_state_machine_1_x, reduced_state_machine_1_y,
       reduced_state_machine_1_z, RST_out;

  Clock CLK (.out(CLK_out));
  LED led_1 (.in(reduced_state_machine_1_w));
  reduced_state_machine reduced_state_machine_1 (
    .W(reduced_state_machine_1_w), .G(G), .X(reduced_state_machine_1_x), .Clock(CLK_out),
    .Y(reduced_state_machine_1_y), .Reset(RST_out), .Z(reduced_state_machine_1_z));
  LED led_2 (.in(reduced_state_machine_1_x));
  LED led_3 (.in(reduced_state_machine_1_y));
  LED led_4 (.in(reduced_state_machine_1_z));
  Button RST (.out(RST_out));
endmodule

module automatic_tester (
  input  in_1
);

  wire and_2_out, and_3_out, and_5_out, CCLK, CLK, comparator_1_gt, comparator_1_lt, comparator_2_gt,
       comparator_2_lt, comparator_3_gt, comparator_3_lt, comparator_4_gt, d_ff_1_q, d_ff_1_qn, DONE, G,
       NCLK, or_2_out, or_3_out, or_4_out, or_5_out, or_6_out;
  wire [3:0] ANS, OUT1, OUT2;
  wire [7:0] and_4_out, counter_1_q, counter_2_q, rom_1_data, shifter_1_out;

  Clock clock_1 (.out(CLK));
  LED ERROR_S (.in(d_ff_1_q));
  LED u_DONE (.in(and_5_out));
  or or_1 (NCLK, CLK, DONE);
  Counter counter_1 (.Q(counter_1_q), .clk(NCLK), .clr(in_1));  // open: load, D, count, carry
  Counter #(.max('h11)) counter_2 (.Q(counter_2_q), .carry(DONE), .clk(or_2_out), .clr(in_1));  // open: load, D, count
  or or_2 (or_2_out, CLK, DONE);
  Comparator #(.width(4), .mode("unsigned")) comparator_1 (
    .a(ANS), .b(4'b0000), .gt(comparator_1_gt), .lt(comparator_1_lt));  // open: eq
  Comparator #(.width(4), .mode("unsigned")) comparator_2 (
    .a(OUT1), .b(ANS), .gt(comparator_2_gt), .lt(comparator_2_lt));  // open: eq
  or or_3 (or_3_out, comparator_2_gt, comparator_2_lt);
  Comparator #(.width(4), .mode("unsigned")) comparator_3 (
    .a(OUT2), .b(ANS), .gt(comparator_3_gt), .lt(comparator_3_lt));  // open: eq
  or or_4 (or_4_out, comparator_3_gt, comparator_3_lt);
  and and_1 (CCLK, CLK, comparator_4_gt);
  Comparator #(.mode("unsigned")) comparator_4 (.a(counter_1_q), .b(8'h1), .gt(comparator_4_gt));  // open: eq, lt
  or or_5 (or_5_out, comparator_1_gt, comparator_1_lt);
  or or_6 (or_6_out, or_3_out, or_4_out);
  ROM rom_1 (.addr(counter_2_q), .data(rom_1_data), .sel(1'b1));
  and and_2 (and_2_out, ~d_ff_1_q, CLK);  // AND_Gate
  and and_3 (and_3_out, or_5_out, or_6_out);
  one_hot_state_machine one_hot_state_machine_1 (
    .W(OUT1[3]), .G(G), .X(OUT1[2]), .Clock(CLK), .Y(OUT1[1]), .Reset(in_1), .Z(OUT1[0]));
  D_Flip_Flop d_ff_1 (
    .clk(and_2_out), .D(and_3_out), .Q(d_ff_1_q), .Qn(d_ff_1_qn), .preset(1'b0), .en(1'b1), .reset(in_1));
  BitSelector bitselector_1 (.in(rom_1_data), .out(G), .sel(3'b000));
  assign and_4_out = 8'hf0 & rom_1_data;  // AND_Gate and_4, 8 bits wide
  and and_5 (and_5_out, d_ff_1_qn, DONE);
  reduced_state_machine reduced_state_machine_1 (
    .W(OUT2[3]), .G(G), .X(OUT2[2]), .Clock(CCLK), .Y(OUT2[1]), .Reset(in_1), .Z(OUT2[0]));
  Shifter #(.shift("lr")) shifter_1 (.in(and_4_out), .\dist (3'b100), .out(shifter_1_out));
  Bit_Extender #(.out_width(4)) bit_extender_1 (.in(shifter_1_out), .out(ANS));

  // Other names for the same wires on the sheet: RST = in_1

  // Notes on the sheet:
  //   Press Ctrl+k to enable ticks and run the tester. You can press Ctrl+k then Ctrl+r to reset it.
  //   contents of rom_1 (hex, n*v repeats v):
  //   0 41 81 61 a0 41 80 61 a0 40 60 10 11 f1 a1 f0 6f
  //   If there are errors with your circuit, "ERROR(S)" will be red, or there will be blue or red wires present when the tester is DONE running.
endmodule
