// Logisim project lab6.circ as structural Verilog: 4 circuits, main circuit RS latch
module RS_latch (
  input  S,
  input  R,
  output Q
);

  wire and_1_out, and_2_out, not_2_out;

  not not_1 (Q, and_1_out);
  and and_1 (and_1_out, S, not_2_out);
  and and_2 (and_2_out, Q, R);
  not not_2 (not_2_out, and_2_out);
endmodule

module Gated_D_Latch (
  input  D,
  input  WE,
  output Q
);

  wire and_1_out, and_2_out, not_1_out, not_2_out;

  and and_1 (and_1_out, D, WE);
  and and_2 (and_2_out, WE, ~D);  // AND_Gate
  not not_1 (not_1_out, and_1_out);
  RS_latch rs_latch_1 (.S(not_1_out), .R(not_2_out), .Q(Q));
  not not_2 (not_2_out, and_2_out);
endmodule

module D_Flip_Flop (
  input  D,
  input  WE,
  output Q
);

  wire gated_d_latch_1_q, not_1_out, not_2_out;

  not not_1 (not_1_out, WE);
  Gated_D_Latch gated_d_latch_1 (.D(D), .WE(not_1_out), .Q(gated_d_latch_1_q));
  not not_2 (not_2_out, not_1_out);
  Gated_D_Latch gated_d_latch_2 (.D(gated_d_latch_1_q), .WE(not_2_out), .Q(Q));
endmodule

module Register (
  input  [3:0] D,
  input  WE,
  output [3:0] Q
);

  wire and_1_out, CLK_out;

  Clock CLK (.out(CLK_out));
  and and_1 (and_1_out, WE, CLK_out);
  D_Flip_Flop d_ff_1 (.D(D[0]), .WE(and_1_out), .Q(Q[0]));
  D_Flip_Flop d_ff_2 (.D(D[1]), .WE(and_1_out), .Q(Q[1]));
  D_Flip_Flop d_ff_3 (.D(D[2]), .WE(and_1_out), .Q(Q[2]));
  D_Flip_Flop d_ff_4 (.D(D[3]), .WE(and_1_out), .Q(Q[3]));
endmodule
