// Logisim project timedlab1.circ as structural Verilog: 2 circuits, main circuit State Machine
module State_Machine (
  input  CLK,
  input  H,
  input  RST,
  output A,
  output B,
  output C,
  output D
);

  wire and_1_out, and_2_out, and_3_out, and_4_out, and_5_out, and_6_out, and_7_out, and_8_out, and_9_out,
       and_10_out, C0, C1, C2, C3, C4, S0, S1, S2, S3, S4;

  and and_1 (and_1_out, ~S0, ~S1, ~S2, ~S3, ~S4);  // AND_Gate
  and and_2 (and_2_out, S1, ~H);  // AND_Gate
  and and_3 (and_3_out, S3, ~H);  // AND_Gate
  and and_4 (and_4_out, S0, H);
  and and_5 (and_5_out, S4, ~H);  // AND_Gate
  and and_6 (and_6_out, S0, ~H);  // AND_Gate
  and and_7 (and_7_out, S1, H);
  and and_8 (and_8_out, S4, H);
  and and_9 (and_9_out, S3, H);
  and and_10 (and_10_out, S2, ~H);  // AND_Gate
  or or_1 (C0, and_1_out, and_2_out, and_3_out);
  or or_2 (C1, and_4_out, and_5_out);
  or or_3 (C2, and_6_out, and_7_out, and_8_out);
  and and_11 (C3, S2, H);
  or or_4 (C4, and_9_out, and_10_out);
  or or_5 (A, S2, S4);
  or or_6 (B, S3, S1);
  or or_7 (C, S1, S2, S3);
  or or_8 (D, S0, S2, S3, S4);
  Register #(.width(5)) register_1 (
    .D({C4, C3, C2, C1, C0}), .Q({S4, S3, S2, S1, S0}), .clk(CLK), .clr(RST));  // open: en

  // Notes on the sheet:
  //   Implement your state machine here
  //   Moving the input and output pins of this subcircuit will break the tester subcircuit
endmodule

module Tester (
);

  wire and_1_out, and_2_out, and_6_out, and_7_out, and_8_out, and_9_out, and_10_out, and_11_out, and_12_out,
       bitselector_1_out, CLK, comparator_1_eq, comparator_2_eq, comparator_3_gt, comparator_3_lt,
       comparator_4_gt, comparator_4_lt, comparator_5_gt, comparator_5_lt, comparator_6_gt, comparator_7_eq,
       d_ff_1_q, d_ff_2_q, d_ff_2_qn, nor_1_out, or_1_out, or_2_out, or_3_out, or_4_out, or_5_out, or_6_out,
       or_7_out, RST, TEST;
  wire [3:0] bit_extender_1_out, bit_extender_2_out, bit_extender_3_out, state_machine_1_d, state_machine_2_d;
  wire [7:0] and_3_out, and_4_out, and_5_out, counter_1_q, counter_2_q, register_1_q, rom_1_data,
       shifter_1_out;

  Button button_1 (.out(TEST));
  Button button_2 (.out(RST));
  Counter counter_1 (.Q(counter_1_q), .clk(and_1_out), .clr(RST));  // open: load, D, count, carry
  and and_1 (and_1_out, or_1_out, d_ff_1_q);
  or or_1 (or_1_out, comparator_1_eq, CLK);
  D_Flip_Flop d_ff_1 (.clk(TEST), .D(TEST), .Q(d_ff_1_q), .preset(1'b0), .en(1'b1), .reset(RST));  // open: Qn
  LED ERROR_S (.in(and_11_out));
  LED NO_ERRORS (.in(and_12_out));
  ROM rom_1 (.addr(counter_1_q), .data(rom_1_data), .sel(1'b1));
  and and_2 (and_2_out, d_ff_1_q, or_2_out);
  or or_2 (or_2_out, comparator_1_eq, CLK);
  BitSelector bitselector_1 (.in(rom_1_data), .out(bitselector_1_out), .sel(3'b000));
  assign and_3_out = 8'hf0 & rom_1_data;  // AND_Gate and_3, 8 bits wide
  assign and_4_out = 8'hf & rom_1_data;  // AND_Gate and_4, 8 bits wide
  assign and_5_out = 8'hf & rom_1_data;  // AND_Gate and_5, 8 bits wide
  Shifter #(.shift("lr")) shifter_1 (.in(and_3_out), .\dist (3'b100), .out(shifter_1_out));
  Bit_Extender #(.out_width(4)) bit_extender_1 (.in(and_4_out), .out(bit_extender_1_out));
  Bit_Extender #(.out_width(4)) bit_extender_2 (.in(and_5_out), .out(bit_extender_2_out));
  State_Machine state_machine_1 (
    .CLK(and_2_out), .H(bitselector_1_out), .RST(or_3_out), .A(state_machine_1_d[3]),
    .B(state_machine_1_d[2]), .C(state_machine_1_d[1]), .D(state_machine_1_d[0]));
  State_Machine state_machine_2 (
    .CLK(and_7_out), .H(bitselector_1_out), .RST(or_3_out), .A(state_machine_2_d[3]),
    .B(state_machine_2_d[2]), .C(state_machine_2_d[1]), .D(state_machine_2_d[0]));
  Clock clock_1 (.out(CLK));
  Bit_Extender #(.out_width(4)) bit_extender_3 (.in(shifter_1_out), .out(bit_extender_3_out));
  Comparator #(.width(4), .mode("unsigned")) comparator_1 (
    .a(bit_extender_1_out), .b(4'b1111), .eq(comparator_1_eq));  // open: gt, lt
  Counter counter_2 (.Q(counter_2_q), .clk(and_2_out), .clr(or_3_out));  // open: load, D, count, carry
  Comparator #(.width(4), .mode("unsigned")) comparator_2 (
    .a(bit_extender_2_out), .b(4'b0010), .eq(comparator_2_eq));  // open: gt, lt
  Comparator #(.width(4), .mode("unsigned")) comparator_3 (
    .a(bit_extender_3_out), .b(4'b0000), .gt(comparator_3_gt), .lt(comparator_3_lt));  // open: eq
  Comparator #(.width(4), .mode("unsigned")) comparator_4 (
    .a(state_machine_1_d), .b(bit_extender_3_out), .gt(comparator_4_gt), .lt(comparator_4_lt));  // open: eq
  Comparator #(.width(4), .mode("unsigned")) comparator_5 (
    .a(state_machine_2_d), .b(bit_extender_3_out), .gt(comparator_5_gt), .lt(comparator_5_lt));  // open: eq
  Comparator #(.mode("unsigned")) comparator_6 (.a(counter_2_q), .b(8'h1), .gt(comparator_6_gt));  // open: eq, lt
  or or_3 (or_3_out, comparator_2_eq, RST);
  or or_4 (or_4_out, comparator_3_gt, comparator_3_lt);
  or or_5 (or_5_out, comparator_4_gt, comparator_4_lt);
  and and_6 (and_6_out, or_5_out, or_6_out);
  or or_6 (or_6_out, comparator_5_gt, comparator_5_lt);
  and and_7 (and_7_out, and_2_out, comparator_6_gt);
  and and_8 (and_8_out, or_4_out, and_6_out);
  Register register_1 (.D(8'h1), .en(nor_1_out), .Q(register_1_q), .clk(CLK), .clr(RST));
  nor nor_1 (nor_1_out, and_8_out, ~and_8_out);  // NOR_Gate
  and and_9 (and_9_out, ~d_ff_2_q, CLK);  // AND_Gate
  D_Flip_Flop d_ff_2 (
    .clk(and_9_out), .D(and_8_out), .Q(d_ff_2_q), .Qn(d_ff_2_qn), .preset(1'b0), .en(1'b1), .reset(RST));
  Comparator #(.mode("unsigned")) comparator_7 (.a(register_1_q), .b({8{1'b0}}), .eq(comparator_7_eq));  // open: gt, lt
  or or_7 (or_7_out, d_ff_2_q, ~comparator_7_eq);  // OR_Gate
  and and_10 (and_10_out, d_ff_2_qn, comparator_7_eq);
  and and_11 (and_11_out, or_7_out, comparator_1_eq);
  and and_12 (and_12_out, and_10_out, comparator_1_eq);

  // Notes on the sheet:
  //   Press Ctrl+k to enable ticks, then click the TEST button to run the verifier.
  //   contents of rom_1 (hex, n*v repeats v):
  //   0 11 61 b0 90 60 10 b1 71 91 b1 70 11 61 2 0 10 bf
endmodule
